// Logisim project LicznikMod4.circ as structural Verilog: 1 circuit, main circuit main
module main (
  input  in_1,
  input  in_2,
  input  in_3,
  input  in_4,
  input  in_5,
  input  in_6,
  input  in_7,
  input  in_8,
  input  in_9,
  input  in_10,
  input  in_11,
  input  in_12,
  input  in_13,
  input  in_14,
  input  in_15,
  input  in_16,
  input  in_17,
  input  in_18,
  input  in_19,
  input  in_20,
  input  in_21,
  input  in_22,
  input  in_23,
  input  in_24,
  input  in_25,
  input  in_26,
  input  in_27,
  output out_28,
  output out_29,
  output out_30,
  output out_31,
  output out_32,
  output out_33,
  output out_34,
  output out_35
);

  wire and_1_out, and_2_out, and_3_out, and_4_out, and_5_out, and_6_out, and_7_out, and_8_out, and_9_out,
       and_10_out, and_11_out, and_12_out, clock_1_out, d_ff_1_qn, d_ff_2_qn, d_ff_3_qn, d_ff_4_qn, d_ff_6_q,
       d_ff_6_qn, d_ff_7_q, d_ff_7_qn, d_ff_8_qn, d_ff_9_q, d_ff_9_qn, d_ff_10_q, d_ff_10_qn, d_ff_11_q,
       d_ff_11_qn, d_ff_12_q, d_ff_12_qn, d_ff_13_q, d_ff_13_qn, d_ff_14_q, d_ff_14_qn, nand_1_out,
       nand_2_out, nand_3_out, nand_4_out, nand_5_out, nand_6_out, nand_8_out, nand_9_out, nand_10_out,
       nand_12_out, nand_13_out, nor_1_out, not_1_out, not_2_out, or_1_out, or_2_out, or_3_out, or_4_out,
       undriven;
  wire [1:0] counter_2_q;

  D_Flip_Flop d_ff_1 (.clk(undriven), .D(d_ff_1_qn), .Qn(d_ff_1_qn));  // open: Q, preset, reset
  J_K_Flip_Flop #(.Pre_Clr_Positions("LEGACY"), .enable("true")) j_k_ff_1 (
    .J(in_14), .clk(in_13), .K(in_15), .Q(out_33), .Qn(out_34), .en(in_16));  // open: preset, reset
  and and_1 (and_1_out, d_ff_6_q, d_ff_7_qn);
  and and_2 (and_2_out, d_ff_6_qn, d_ff_7_q);
  D_Flip_Flop d_ff_2 (.clk(d_ff_1_qn), .D(d_ff_2_qn), .Qn(d_ff_2_qn));  // open: Q, preset, reset
  T_Flip_Flop t_ff_1 (.clk(in_6), .T(in_8), .Q(out_28), .Qn(out_30), .preset(in_4), .reset(in_10));
  ROM #(.addrWidth(7), .dataWidth(10), .Select("low")) rom_1 ();  // open: addr, data
  or or_1 (or_1_out, and_1_out, and_2_out);
  Clock clock_1 (.out(clock_1_out));
  Counter #(.width(4), .max('h3)) counter_1 (.clk(nor_1_out));  // open: load, D, count, Q, carry, clr, preset, down
  Counter #(.width(2), .max('h3)) counter_2 (
    .Q(counter_2_q), .clk(in_27));  // open: load, D, count, carry, clr, preset, down
  D_Flip_Flop d_ff_3 (.clk(d_ff_2_qn), .D(d_ff_3_qn), .Qn(d_ff_3_qn));  // open: Q, preset, reset
  nor nor_1 (nor_1_out, counter_2_q[0], counter_2_q[1]);
  D_Flip_Flop d_ff_4 (.clk(d_ff_3_qn), .D(d_ff_4_qn), .Qn(d_ff_4_qn));  // open: Q, preset, reset
  D_Flip_Flop d_ff_5 (.clk(in_7), .D(in_9), .Q(out_29), .Qn(out_31), .preset(in_5), .reset(in_11));
  D_Flip_Flop d_ff_6 (.clk(clock_1_out), .D(or_1_out), .Q(d_ff_6_q), .Qn(d_ff_6_qn), .preset(in_19), .reset(not_2_out));
  D_Flip_Flop d_ff_7 (
    .clk(clock_1_out), .D(d_ff_7_qn), .Q(d_ff_7_q), .Qn(d_ff_7_qn), .preset(in_23), .reset(not_2_out));
  D_Flip_Flop d_ff_8 (.clk(d_ff_4_qn), .D(d_ff_8_qn), .Qn(d_ff_8_qn));  // open: Q, preset, reset
  and and_3 (and_3_out, d_ff_9_q, d_ff_10_qn);
  and and_4 (and_4_out, d_ff_9_qn, d_ff_10_q);
  or or_2 (or_2_out, and_3_out, and_4_out);
  and and_5 (and_5_out, d_ff_6_qn, d_ff_7_qn);
  nand nand_1 (nand_1_out, in_1, in_1);
  nand nand_2 (nand_2_out, in_2, in_2);
  nand nand_3 (nand_3_out, in_17, in_17);
  nand nand_4 (nand_4_out, in_18, in_18);
  nand nand_5 (nand_5_out, in_3, in_3);
  nand nand_6 (nand_6_out, nand_3_out, nand_4_out);
  D_Flip_Flop d_ff_9 (.clk(and_5_out), .D(or_2_out), .Q(d_ff_9_q), .Qn(d_ff_9_qn), .preset(in_20), .reset(not_2_out));
  D_Flip_Flop d_ff_10 (
    .clk(and_5_out), .D(d_ff_10_qn), .Q(d_ff_10_q), .Qn(d_ff_10_qn), .preset(in_24), .reset(not_2_out));
  nand nand_7 (out_35, nand_6_out, nand_6_out);
  nand nand_8 (nand_8_out, nand_5_out, in_2, in_1);
  nand nand_9 (nand_9_out, in_3, nand_2_out, in_1);
  nand nand_10 (nand_10_out, in_3, in_2, nand_1_out);
  nand nand_11 (out_32, nand_8_out, nand_9_out, nand_10_out);
  and and_6 (and_6_out, d_ff_11_q, d_ff_12_qn);
  and and_7 (and_7_out, d_ff_11_qn, d_ff_12_q);
  or or_3 (or_3_out, and_6_out, and_7_out);
  and and_8 (and_8_out, d_ff_9_qn, d_ff_10_qn);
  not not_1 (not_1_out, clock_1_out);
  D_Flip_Flop d_ff_11 (
    .clk(and_8_out), .D(or_3_out), .Q(d_ff_11_q), .Qn(d_ff_11_qn), .preset(in_21), .reset(not_2_out));
  D_Flip_Flop d_ff_12 (
    .clk(and_8_out), .D(d_ff_12_qn), .Q(d_ff_12_q), .Qn(d_ff_12_qn), .preset(in_25), .reset(not_2_out));
  and and_9 (and_9_out, d_ff_13_q, d_ff_14_qn);
  or or_4 (or_4_out, and_9_out, and_10_out);
  and and_10 (and_10_out, d_ff_13_qn, d_ff_14_q);
  and and_11 (and_11_out, d_ff_11_qn, d_ff_12_qn);
  D_Flip_Flop d_ff_13 (
    .clk(and_11_out), .D(or_4_out), .Q(d_ff_13_q), .Qn(d_ff_13_qn), .preset(in_22), .reset(not_2_out));
  D_Flip_Flop d_ff_14 (
    .clk(and_11_out), .D(d_ff_14_qn), .Q(d_ff_14_q), .Qn(d_ff_14_qn), .preset(in_26), .reset(not_2_out));
  not not_2 (not_2_out, nand_12_out);
  and and_12 (and_12_out, d_ff_7_q, d_ff_10_q, d_ff_11_q, d_ff_14_q);
  nand nand_12 (nand_12_out, and_12_out, nand_13_out);
  nand nand_13 (nand_13_out, nand_12_out, not_1_out);

  // Notes on the sheet:
  //   contents of rom_1 (hex, n*v repeats v):
  //   199
endmodule
