// Logisim project pomocnaukowa.circ as structural Verilog: 1 circuit, main circuit main
module main (
  input  in_1,
  input  in_2,
  input  in_3,
  input  in_4,
  input  in_5,
  input  in_6,
  input  in_7,
  input  in_8,
  input  in_9,
  input  in_10,
  input  in_11,
  input  in_12,
  input  in_13,
  input  Binary_to_Gray,
  input  in_15,
  input  in_16,
  input  in_17,
  input  in_18,
  input  in_19,
  input  in_20,
  input  in_21,
  input  in_22,
  input  in_23,
  input  in_24,
  input  in_25,
  input  in_26,
  input  in_27,
  input  in_28,
  input  in_29,
  input  in_30,
  input  in_31,
  input  in_32,
  output out_33,
  output out_34,
  output out_35,
  output out_36,
  output out_37,
  output out_38,
  output out_39,
  output out_40,
  output out_41,
  output out_42,
  output out_43,
  output out_44
);

  wire and_1_out, and_2_out, and_3_out, and_4_out, and_5_out, and_6_out, and_7_out, and_8_out, and_9_out,
       and_10_out, clock_1_out, clock_2_out, clock_3_out, clock_4_out, clock_5_out, clock_6_out, d_ff_1_q,
       d_ff_2_q, d_ff_2_qn, d_ff_3_qn, d_ff_4_qn, d_ff_5_qn, d_ff_6_qn, d_ff_7_qn, d_ff_8_q, d_ff_8_qn,
       d_ff_9_q, d_ff_9_qn, d_ff_10_q, d_ff_10_qn, d_ff_11_q, d_ff_11_qn, d_ff_12_q, d_ff_12_qn, d_ff_13_q,
       d_ff_13_qn, d_ff_14_qn, j_k_ff_3_q, j_k_ff_4_q, j_k_ff_5_q, j_k_ff_6_q, not_1_out, not_2_out,
       not_3_out, not_4_out, not_5_out, or_1_out, or_2_out, or_3_out, or_4_out, t_ff_2_qn, t_ff_3_qn,
       t_ff_4_q, t_ff_4_qn, t_ff_5_q, t_ff_5_qn, t_ff_6_qn, t_ff_7_qn, t_ff_8_qn, t_ff_9_qn, t_ff_10_qn,
       t_ff_11_q, t_ff_12_q, t_ff_13_q, t_ff_14_q;

  not not_1 (not_1_out, in_5);
  and and_1 (and_1_out, not_1_out, d_ff_1_q);
  and and_2 (and_2_out, in_3, not_2_out);
  not not_2 (not_2_out, d_ff_1_q);
  and and_3 (and_3_out, in_3, not_3_out);
  not not_3 (not_3_out, in_5);
  or or_1 (or_1_out, and_1_out, and_2_out, and_3_out);
  J_K_Flip_Flop j_k_ff_1 (.J(in_9), .clk(in_6), .K(in_9));  // open: Q, Qn, preset, reset
  D_Flip_Flop d_ff_1 (.clk(in_1), .D(or_1_out), .Q(d_ff_1_q));  // open: Qn, preset, reset
  T_Flip_Flop t_ff_1 (.clk(in_7), .T(in_10));  // open: Q, Qn, preset, reset
  T_Flip_Flop t_ff_2 (.clk(in_8), .T(1'b1), .Qn(t_ff_2_qn));  // open: Q, preset, reset
  xor xor_1 (out_34, in_12, in_15);
  and and_4 (and_4_out, d_ff_2_qn, in_4);
  not not_4 (not_4_out, in_4);
  and and_5 (and_5_out, not_4_out, d_ff_2_q);
  T_Flip_Flop t_ff_3 (.clk(t_ff_2_qn), .T(1'b1), .Qn(t_ff_3_qn));  // open: Q, preset, reset
  xor xor_2 (out_36, out_34, in_16);
  xor xor_3 (out_38, out_36, in_18);
  D_Flip_Flop d_ff_2 (.clk(in_2), .D(or_2_out), .Q(d_ff_2_q), .Qn(d_ff_2_qn));  // open: preset, reset
  or or_2 (or_2_out, and_4_out, and_5_out);
  T_Flip_Flop t_ff_4 (.clk(t_ff_3_qn), .T(1'b1), .Q(t_ff_4_q), .Qn(t_ff_4_qn), .reset(and_6_out));  // open: preset
  T_Flip_Flop t_ff_5 (.clk(t_ff_4_qn), .T(1'b1), .Q(t_ff_5_q), .Qn(t_ff_5_qn), .reset(and_6_out));  // open: preset
  and and_6 (and_6_out, t_ff_4_q, t_ff_5_q);
  xor xor_4 (out_37, Binary_to_Gray, in_17);
  xor xor_5 (out_39, in_17, in_19);
  xor xor_6 (out_40, in_19, in_20);
  Clock clock_1 (.out(clock_1_out));
  Clock clock_2 (.out(clock_2_out));
  D_Flip_Flop d_ff_3 (.clk(clock_1_out), .D(d_ff_3_qn), .Qn(d_ff_3_qn), .reset(in_11));  // open: Q, preset
  T_Flip_Flop t_ff_6 (.clk(clock_2_out), .T(1'b1), .Qn(t_ff_6_qn), .reset(in_11));  // open: Q, preset
  Counter counter_1 (.clk(clock_3_out));  // open: load, D, count, Q, carry, clr, preset, down
  Clock clock_3 (.out(clock_3_out));
  D_Flip_Flop d_ff_4 (.clk(d_ff_3_qn), .D(d_ff_4_qn), .Qn(d_ff_4_qn), .reset(in_11));  // open: Q, preset
  T_Flip_Flop t_ff_7 (.clk(t_ff_6_qn), .T(1'b1), .Qn(t_ff_7_qn), .reset(in_11));  // open: Q, preset
  S_R_Flip_Flop s_r_ff_1 (.S(in_25), .clk(in_23), .R(in_27), .Q(out_41), .Qn(out_43), .preset(in_21), .reset(in_29));
  not not_5 (not_5_out, in_31);
  D_Flip_Flop d_ff_5 (.clk(d_ff_4_qn), .D(d_ff_5_qn), .Qn(d_ff_5_qn), .reset(in_11));  // open: Q, preset
  T_Flip_Flop t_ff_8 (.clk(t_ff_7_qn), .T(1'b1), .Qn(t_ff_8_qn), .reset(in_11));  // open: Q, preset
  and and_7 (and_7_out, d_ff_8_qn, d_ff_9_qn, not_5_out);
  and and_8 (and_8_out, d_ff_9_q, in_31);
  D_Flip_Flop d_ff_6 (.clk(d_ff_5_qn), .D(d_ff_6_qn), .Qn(d_ff_6_qn), .reset(in_11));  // open: Q, preset
  T_Flip_Flop t_ff_9 (.clk(t_ff_8_qn), .T(1'b1), .Qn(t_ff_9_qn), .reset(in_11));  // open: Q, preset
  J_K_Flip_Flop j_k_ff_2 (.J(in_26), .clk(in_24), .K(in_28), .Q(out_42), .Qn(out_44), .preset(in_22), .reset(in_30));
  or or_3 (or_3_out, and_7_out, and_8_out);
  and and_9 (and_9_out, d_ff_8_qn, d_ff_9_qn, in_31);
  or or_4 (or_4_out, and_9_out, and_10_out);
  and and_10 (and_10_out, d_ff_8_q, not_5_out);
  D_Flip_Flop d_ff_7 (.clk(d_ff_6_qn), .D(d_ff_7_qn), .Qn(d_ff_7_qn), .reset(in_11));  // open: Q, preset
  T_Flip_Flop t_ff_10 (.clk(t_ff_9_qn), .T(1'b1), .Qn(t_ff_10_qn), .reset(in_11));  // open: Q, preset
  D_Flip_Flop d_ff_8 (.clk(in_32), .D(or_3_out), .Q(d_ff_8_q), .Qn(d_ff_8_qn));  // open: preset, reset
  D_Flip_Flop d_ff_9 (.clk(in_32), .D(or_4_out), .Q(d_ff_9_q), .Qn(d_ff_9_qn));  // open: preset, reset
  Clock clock_4 (.out(clock_4_out));
  Clock clock_5 (.out(clock_5_out));
  Clock clock_6 (.out(clock_6_out));
  D_Flip_Flop d_ff_10 (
    .clk(clock_4_out), .D(d_ff_10_qn), .Q(d_ff_10_q), .Qn(d_ff_10_qn), .reset(in_13));  // open: preset
  T_Flip_Flop t_ff_11 (.clk(clock_5_out), .T(1'b1), .Q(t_ff_11_q), .reset(in_13));  // open: Qn, preset
  J_K_Flip_Flop j_k_ff_3 (.J(1'b1), .clk(clock_6_out), .K(1'b1), .Q(j_k_ff_3_q), .reset(in_13));  // open: Qn, preset
  D_Flip_Flop d_ff_11 (.clk(d_ff_10_q), .D(d_ff_11_qn), .Q(d_ff_11_q), .Qn(d_ff_11_qn), .reset(in_13));  // open: preset
  T_Flip_Flop t_ff_12 (.clk(t_ff_11_q), .T(1'b1), .Q(t_ff_12_q), .reset(in_13));  // open: Qn, preset
  J_K_Flip_Flop j_k_ff_4 (.J(1'b1), .clk(j_k_ff_3_q), .K(1'b1), .Q(j_k_ff_4_q), .reset(in_13));  // open: Qn, preset
  D_Flip_Flop d_ff_12 (.clk(d_ff_11_q), .D(d_ff_12_qn), .Q(d_ff_12_q), .Qn(d_ff_12_qn), .reset(in_13));  // open: preset
  T_Flip_Flop t_ff_13 (.clk(t_ff_12_q), .T(1'b1), .Q(t_ff_13_q), .reset(in_13));  // open: Qn, preset
  J_K_Flip_Flop j_k_ff_5 (.J(1'b1), .clk(j_k_ff_4_q), .K(1'b1), .Q(j_k_ff_5_q), .reset(in_13));  // open: Qn, preset
  D_Flip_Flop d_ff_13 (.clk(d_ff_12_q), .D(d_ff_13_qn), .Q(d_ff_13_q), .Qn(d_ff_13_qn), .reset(in_13));  // open: preset
  T_Flip_Flop t_ff_14 (.clk(t_ff_13_q), .T(1'b1), .Q(t_ff_14_q), .reset(in_13));  // open: Qn, preset
  J_K_Flip_Flop j_k_ff_6 (.J(1'b1), .clk(j_k_ff_5_q), .K(1'b1), .Q(j_k_ff_6_q), .reset(in_13));  // open: Qn, preset
  D_Flip_Flop d_ff_14 (.clk(d_ff_13_q), .D(d_ff_14_qn), .Qn(d_ff_14_qn), .reset(in_13));  // open: Q, preset
  T_Flip_Flop t_ff_15 (.clk(t_ff_14_q), .T(1'b1), .reset(in_13));  // open: Q, Qn, preset
  J_K_Flip_Flop j_k_ff_7 (.J(1'b1), .clk(j_k_ff_6_q), .K(1'b1), .reset(in_13));  // open: Q, Qn, preset

  assign out_33 = in_12;
  assign out_35 = Binary_to_Gray;

  // Notes on the sheet:
  //   Gray to Binary
endmodule
