// Logisim project zadanie2.circ as structural Verilog: 1 circuit, main circuit main
module main (
  input  in_1
);

  wire clock_1_out, t_ff_1_q, t_ff_1_qn, t_ff_2_qn, t_ff_3_qn, t_ff_4_q, t_ff_4_qn, t_ff_5_qn, t_ff_6_qn,
       t_ff_7_q, t_ff_7_qn, t_ff_8_q, t_ff_8_qn;

  Clock clock_1 (.out(clock_1_out));
  T_Flip_Flop t_ff_1 (.clk(clock_1_out), .T(1'b1), .Q(t_ff_1_q), .Qn(t_ff_1_qn), .reset(in_1));  // open: preset
  T_Flip_Flop t_ff_2 (.clk(t_ff_1_qn), .T(1'b1), .Qn(t_ff_2_qn), .reset(in_1));  // open: Q, preset
  T_Flip_Flop t_ff_3 (.clk(t_ff_2_qn), .T(1'b1), .Qn(t_ff_3_qn), .reset(in_1));  // open: Q, preset
  T_Flip_Flop t_ff_4 (.clk(t_ff_3_qn), .T(1'b1), .Q(t_ff_4_q), .Qn(t_ff_4_qn), .reset(in_1));  // open: preset
  T_Flip_Flop t_ff_5 (.clk(t_ff_4_qn), .T(1'b1), .Qn(t_ff_5_qn), .reset(in_1));  // open: Q, preset
  T_Flip_Flop t_ff_6 (.clk(t_ff_5_qn), .T(1'b1), .Qn(t_ff_6_qn), .reset(in_1));  // open: Q, preset
  // NOT_Gate not_1 is placed but not wired
  T_Flip_Flop t_ff_7 (.clk(t_ff_6_qn), .T(1'b1), .Q(t_ff_7_q), .Qn(t_ff_7_qn), .reset(in_1));  // open: preset
  T_Flip_Flop t_ff_8 (.clk(t_ff_7_qn), .T(1'b1), .Q(t_ff_8_q), .Qn(t_ff_8_qn), .reset(in_1));  // open: preset
  and and_1 (in_1, t_ff_1_q, t_ff_4_q, t_ff_7_q, t_ff_8_q);
  T_Flip_Flop t_ff_9 (.clk(t_ff_8_qn), .T(1'b1), .reset(in_1));  // open: Q, Qn, preset
endmodule
