// Logisim project zadanie4.circ as structural Verilog: 1 circuit, main circuit main
module main (
);

  wire and_1_out, and_2_out, clock_1_out, t_ff_1_qn, t_ff_2_qn, t_ff_3_q, t_ff_3_qn, t_ff_4_q, t_ff_5_qn,
       t_ff_6_q, t_ff_6_qn, t_ff_7_qn, t_ff_8_q, t_ff_8_qn, t_ff_9_qn, t_ff_10_q, t_ff_10_qn;

  Clock clock_1 (.out(clock_1_out));
  T_Flip_Flop t_ff_1 (.clk(clock_1_out), .T(1'b1), .Qn(t_ff_1_qn), .reset(and_1_out));  // open: Q, preset
  T_Flip_Flop t_ff_2 (.clk(t_ff_10_qn), .T(1'b1), .Qn(t_ff_2_qn), .reset(t_ff_4_q));  // open: Q, preset
  T_Flip_Flop t_ff_3 (.clk(t_ff_1_qn), .T(1'b1), .Q(t_ff_3_q), .Qn(t_ff_3_qn), .reset(and_1_out));  // open: preset
  T_Flip_Flop t_ff_4 (.clk(t_ff_2_qn), .T(1'b1), .Q(t_ff_4_q), .reset(t_ff_4_q));  // open: Qn, preset
  T_Flip_Flop t_ff_5 (.clk(t_ff_3_qn), .T(1'b1), .Qn(t_ff_5_qn), .reset(and_1_out));  // open: Q, preset
  T_Flip_Flop t_ff_6 (.clk(t_ff_5_qn), .T(1'b1), .Q(t_ff_6_q), .Qn(t_ff_6_qn), .reset(and_1_out));  // open: preset
  D_Flip_Flop d_ff_1 ();  // open: clk, D, Q, Qn, preset, reset
  D_Flip_Flop d_ff_2 ();  // open: clk, D, Q, Qn, preset, reset
  D_Flip_Flop d_ff_3 ();  // open: clk, D, Q, Qn, preset, reset
  D_Flip_Flop d_ff_4 ();  // open: clk, D, Q, Qn, preset, reset
  and and_1 (and_1_out, t_ff_3_q, t_ff_6_q);
  T_Flip_Flop t_ff_7 (.clk(t_ff_6_qn), .T(1'b1), .Qn(t_ff_7_qn), .reset(and_2_out));  // open: Q, preset
  T_Flip_Flop t_ff_8 (.clk(t_ff_7_qn), .T(1'b1), .Q(t_ff_8_q), .Qn(t_ff_8_qn), .reset(and_2_out));  // open: preset
  T_Flip_Flop t_ff_9 (.clk(t_ff_8_qn), .T(1'b1), .Qn(t_ff_9_qn), .reset(and_2_out));  // open: Q, preset
  T_Flip_Flop t_ff_10 (.clk(t_ff_9_qn), .T(1'b1), .Q(t_ff_10_q), .Qn(t_ff_10_qn), .reset(and_2_out));  // open: preset
  and and_2 (and_2_out, t_ff_8_q, t_ff_10_q);
endmodule
