// Logisim project Laby1.circ as structural Verilog: 1 circuit, main circuit main
module main (
  input  in_1,
  input  in_2,
  input  in_3,
  input  in_4,
  input  in_5,
  input  in_6,
  output out_7,
  output out_8
);

  wire and_1_out, and_2_out, and_3_out, nand_1_out, nand_2_out, nand_3_out, not_1_out, not_2_out, not_3_out,
       undriven, undriven_2, undriven_3;

  not not_1 (not_1_out, in_1);
  not not_2 (not_2_out, in_2);
  not not_3 (not_3_out, in_3);
  and and_1 (and_1_out, not_1_out, in_2, in_3);
  and and_2 (and_2_out, in_1, not_2_out, in_3);
  and and_3 (and_3_out, in_1, in_2, not_3_out);
  nand nand_1 (nand_1_out, undriven, in_5, in_6);
  nand nand_2 (nand_2_out, in_4, undriven_2, in_6);
  nand nand_3 (nand_3_out, in_4, in_5, undriven_3);
  or or_1 (out_7, and_1_out, and_2_out, and_3_out);
  LED led_1 (.in(out_7));
  LED led_2 (.in(out_8));
  nand nand_4 (out_8, nand_1_out, nand_2_out, nand_3_out);
endmodule
