// Logisim project Sprawozdanie1_Realizacja.circ as structural Verilog: 1 circuit, main circuit main
module main (
  input  X1,
  input  X2,
  input  X3,
  output Y1,
  output Y2,
  output Y3
);

  wire and_1_out, not_1_out, not_2_out, not_3_out, not_4_out;

  not not_1 (not_1_out, X1);
  not not_2 (not_2_out, X1);
  and and_1 (and_1_out, not_2_out, X2, X3);
  not not_3 (not_3_out, X2);
  not not_4 (not_4_out, X3);
  and and_2 (Y1, not_1_out, X2);
  or or_1 (Y2, X1, and_1_out);
  and and_3 (Y3, not_3_out, not_4_out);
endmodule
