// Logisim project Zadanie1.circ as structural Verilog: 1 circuit, main circuit main
// ADDRESS
module main (
  input  A0,
  input  A1,
  input  A2,
  input  A3,
  input  MR,
  input  MW,
  input  IOR,
  input  IOW,
  input  K1,
  input  in_10,
  input  in_11,
  input  in_12
);

  wire and_1_out, and_2_out, and_3_out, demultiplexer_1_out4, demultiplexer_1_out8, demultiplexer_1_out9,
       nand_1_out, nand_2_out, not_1_out, not_2_out, not_3_out, not_4_out, not_5_out;
  wire [3:0] controlled_buffer_1_out, ram_1_data, RD_q, W0_q, W1_q;

  Register #(.width(4), .trigger("high"), .Select("low")) RD (
    .D(controlled_buffer_1_out), .Q(RD_q), .clk(nand_1_out));  // open: en, clr
  assign controlled_buffer_1_out = nand_2_out ? RD_q : 4'bz;  // Controlled_Buffer controlled_buffer_1
  nand nand_1 (nand_1_out, IOR, MR);
  nand nand_2 (nand_2_out, IOW, MW);
  not not_1 (not_1_out, MR);
  RAM #(.addrWidth(4), .dataWidth(4), .bus("asynch"), .Select("high")) ram_1 (
    .addr({A3, A2, A1, A0}), .data(ram_1_data), .ld(MW));  // open: sel, clr
  not not_2 (not_2_out, MW);
  assign controlled_buffer_1_out = not_1_out ? ram_1_data : 4'bz;  // Controlled_Buffer controlled_buffer_2
  assign ram_1_data = not_2_out ? controlled_buffer_1_out : 4'bz;  // Controlled_Buffer controlled_buffer_3
  Demultiplexer #(.select(4)) demultiplexer_1 (
    .out4(demultiplexer_1_out4), .out8(demultiplexer_1_out8), .out9(demultiplexer_1_out9), .in(1'b1),
    .sel({A3, A2, A1, A0}));  // open: out0, out1, out2, out3, out5, out6, out7, out10, out11, out12, out13, out14, out15, en
  not not_3 (not_3_out, IOR);
  and and_1 (and_1_out, not_3_out, demultiplexer_1_out4);
  assign controlled_buffer_1_out = and_1_out ? {K1, in_10, in_11, in_12} : 4'bz;  // Controlled_Buffer controlled_buffer_4
  not not_4 (not_4_out, IOW);
  not not_5 (not_5_out, IOW);
  Hex_Digit_Display hex_digit_display_1 (.value(W1_q));  // open: dp
  Register #(.width(4), .trigger("high"), .Select("low")) W1 (
    .D(controlled_buffer_1_out), .Q(W1_q), .clk(and_2_out));  // open: en, clr
  and and_2 (and_2_out, not_4_out, demultiplexer_1_out9);
  and and_3 (and_3_out, not_5_out, demultiplexer_1_out8);
  Hex_Digit_Display hex_digit_display_2 (.value(W0_q));  // open: dp
  Register #(.width(4), .trigger("high"), .Select("low")) W0 (
    .D(controlled_buffer_1_out), .Q(W0_q), .clk(and_3_out));  // open: en, clr
  Hex_Digit_Display hex_digit_display_3 (.value({A3, A2, A1, A0}));  // open: dp
  Hex_Digit_Display hex_digit_display_4 (.value(controlled_buffer_1_out));  // open: dp

  // Notes on the sheet:
  //   DATA
  //   ADDRESS
endmodule
