// Logisim project Zadanie2.circ as structural Verilog: 1 circuit, main circuit main
module main (
  input  in_1,
  input  in_2,
  input  in_3,
  input  in_4,
  output out_5,
  output out_6,
  output out_7,
  output out_8
);

  ROM #(.addrWidth(4), .dataWidth(4), .Select("low")) rom_1 (
    .addr({in_4, in_3, in_2, in_1}), .data({out_8, out_7, out_6, out_5}));

  // Notes on the sheet:
  //   contents of rom_1 (hex, n*v repeats v):
  //   3 4 2 0 9 5 d e 8 a b c f 6 7
endmodule
