// Logisim project Zadanie3.circ as structural Verilog: 1 circuit, main circuit main
module main (
  input  in_1,
  input  in_2,
  input  in_3,
  input  in_4,
  input  in_5,
  input  in_6,
  input  in_7,
  input  in_8,
  input  IOW_tilde,
  output out_10
);

  wire and_1_out, not_1_out, not_2_out, not_3_out, not_4_out, not_5_out, not_6_out;

  not not_1 (not_1_out, in_2);
  not not_2 (not_2_out, in_3);
  not not_3 (not_3_out, in_4);
  not not_4 (not_4_out, in_5);
  not not_5 (not_5_out, in_6);
  and and_1 (and_1_out, in_1, not_1_out, not_2_out, not_3_out, not_4_out, not_5_out, in_7, in_8);
  not not_6 (not_6_out, IOW_tilde);
  and and_2 (out_10, not_6_out, and_1_out);

  // Notes on the sheet:
  //   Układ 1. Dekoder adresu. 
  //   Układ 2. Sterowanie wpisem.
endmodule
