// Logisim project Zadanie22.circ as structural Verilog: 1 circuit, main circuit main
module main (
  input  in_1
);

  wire and_1_out, and_2_out, and_3_out, and_4_out, d_ff_1_q, d_ff_1_qn, d_ff_2_q, d_ff_2_qn, d_ff_3_q,
       d_ff_3_qn, or_1_out, or_2_out;

  and and_1 (and_1_out, d_ff_3_qn, d_ff_1_q);
  and and_2 (and_2_out, d_ff_3_qn, d_ff_2_q);
  and and_3 (and_3_out, d_ff_3_q, d_ff_1_qn, d_ff_2_qn);
  and and_4 (and_4_out, d_ff_3_q, d_ff_2_q);
  or or_1 (or_1_out, and_1_out, and_2_out);
  or or_2 (or_2_out, and_3_out, and_4_out);
  D_Flip_Flop d_ff_1 (.clk(in_1), .D(d_ff_3_qn), .Q(d_ff_1_q), .Qn(d_ff_1_qn));  // open: preset, reset
  D_Flip_Flop d_ff_2 (.clk(in_1), .D(or_2_out), .Q(d_ff_2_q), .Qn(d_ff_2_qn));  // open: preset, reset
  D_Flip_Flop d_ff_3 (.clk(in_1), .D(or_1_out), .Q(d_ff_3_q), .Qn(d_ff_3_qn));  // open: preset, reset
endmodule
