// Logisim project Zadanie23.circ as structural Verilog: 1 circuit, main circuit main
module main (
  input  in_1,
  input  in_2,
  input  in_3,
  input  in_4,
  input  in_5,
  input  in_6,
  input  in_7,
  input  in_8,
  input  in_9,
  input  in_10,
  input  in_11,
  input  in_12,
  input  in_13,
  input  in_14,
  input  in_15,
  input  in_16,
  input  in_17,
  input  in_18,
  output out_19,
  output out_20,
  output out_21,
  output out_22,
  output out_23,
  output out_24,
  output out_25,
  output out_26
);

  wire d_ff_1_qn, d_ff_2_qn, d_ff_3_qn, d_ff_4_qn, d_ff_6_qn, nand_1_out, nand_2_out, nand_3_out, nand_4_out,
       nand_5_out, nand_6_out, nand_8_out, nand_9_out, nand_10_out, undriven;

  D_Flip_Flop d_ff_1 (.clk(undriven), .D(d_ff_1_qn), .Qn(d_ff_1_qn));  // open: Q, preset, reset
  J_K_Flip_Flop #(.Pre_Clr_Positions("LEGACY"), .enable("true")) j_k_ff_1 (
    .J(in_14), .clk(in_13), .K(in_15), .Q(out_24), .Qn(out_25), .en(in_16));  // open: preset, reset
  D_Flip_Flop d_ff_2 (.clk(d_ff_1_qn), .D(d_ff_2_qn), .Qn(d_ff_2_qn));  // open: Q, preset, reset
  T_Flip_Flop t_ff_1 (.clk(in_6), .T(in_8), .Q(out_19), .Qn(out_21), .preset(in_4), .reset(in_10));
  ROM #(.addrWidth(7), .dataWidth(10), .Select("low")) rom_1 ();  // open: addr, data
  D_Flip_Flop d_ff_3 (.clk(d_ff_2_qn), .D(d_ff_3_qn), .Qn(d_ff_3_qn));  // open: Q, preset, reset
  D_Flip_Flop d_ff_4 (.clk(d_ff_3_qn), .D(d_ff_4_qn), .Qn(d_ff_4_qn));  // open: Q, preset, reset
  D_Flip_Flop d_ff_5 (.clk(in_7), .D(in_9), .Q(out_20), .Qn(out_22), .preset(in_5), .reset(in_11));
  D_Flip_Flop d_ff_6 (.clk(d_ff_4_qn), .D(d_ff_6_qn), .Qn(d_ff_6_qn));  // open: Q, preset, reset
  nand nand_1 (nand_1_out, in_2, in_2);
  nand nand_2 (nand_2_out, in_1, in_1);
  nand nand_3 (nand_3_out, in_17, in_17);
  nand nand_4 (nand_4_out, in_18, in_18);
  nand nand_5 (nand_5_out, in_3, in_3);
  nand nand_6 (nand_6_out, nand_3_out, nand_4_out);
  nand nand_7 (out_26, nand_6_out, nand_6_out);
  nand nand_8 (nand_8_out, nand_5_out, in_2, in_1);
  nand nand_9 (nand_9_out, in_3, nand_1_out, in_1);
  nand nand_10 (nand_10_out, in_3, in_2, nand_2_out);
  nand nand_11 (out_23, nand_8_out, nand_9_out, nand_10_out);

  // Notes on the sheet:
  //   contents of rom_1 (hex, n*v repeats v):
  //   199
endmodule
