// Logisim project Licznik24h.circ as structural Verilog: 1 circuit, main circuit main
module main (
);

  wire and_1_out, and_2_out, and_3_out, and_4_out, clock_1_out, or_1_out, t_ff_1_qn, t_ff_2_qn, t_ff_3_qn,
       t_ff_4_qn, t_ff_5_qn, t_ff_6_qn, t_ff_7_qn, t_ff_9_qn, t_ff_11_qn, t_ff_12_qn;
  wire [1:0] t_ff_12_q;
  wire [2:0] t_ff_2_q;
  wire [3:0] t_ff_1_q, t_ff_3_q;

  Clock clock_1 (.out(clock_1_out));
  T_Flip_Flop t_ff_1 (.clk(clock_1_out), .T(1'b1), .Q(t_ff_1_q[0]), .Qn(t_ff_1_qn), .reset(and_1_out));  // open: preset
  T_Flip_Flop t_ff_2 (.clk(and_1_out), .T(1'b1), .Q(t_ff_2_q[0]), .Qn(t_ff_2_qn), .reset(and_2_out));  // open: preset
  T_Flip_Flop t_ff_3 (.clk(and_2_out), .T(1'b1), .Q(t_ff_3_q[0]), .Qn(t_ff_3_qn), .reset(or_1_out));  // open: preset
  T_Flip_Flop t_ff_4 (.clk(t_ff_1_qn), .T(1'b1), .Q(t_ff_1_q[1]), .Qn(t_ff_4_qn), .reset(and_1_out));  // open: preset
  T_Flip_Flop t_ff_5 (.clk(t_ff_2_qn), .T(1'b1), .Q(t_ff_2_q[1]), .Qn(t_ff_5_qn), .reset(and_2_out));  // open: preset
  T_Flip_Flop t_ff_6 (.clk(t_ff_3_qn), .T(1'b1), .Q(t_ff_3_q[1]), .Qn(t_ff_6_qn), .reset(or_1_out));  // open: preset
  T_Flip_Flop t_ff_7 (.clk(t_ff_4_qn), .T(1'b1), .Q(t_ff_1_q[2]), .Qn(t_ff_7_qn), .reset(and_1_out));  // open: preset
  T_Flip_Flop t_ff_8 (.clk(t_ff_5_qn), .T(1'b1), .Q(t_ff_2_q[2]), .reset(and_2_out));  // open: Qn, preset
  T_Flip_Flop t_ff_9 (.clk(t_ff_6_qn), .T(1'b1), .Q(t_ff_3_q[2]), .Qn(t_ff_9_qn), .reset(or_1_out));  // open: preset
  and and_1 (and_1_out, t_ff_1_q[1], t_ff_1_q[3]);
  T_Flip_Flop t_ff_10 (.clk(t_ff_7_qn), .T(1'b1), .Q(t_ff_1_q[3]), .reset(and_1_out));  // open: Qn, preset
  and and_2 (and_2_out, t_ff_2_q[1], t_ff_2_q[2]);
  T_Flip_Flop t_ff_11 (.clk(t_ff_9_qn), .T(1'b1), .Q(t_ff_3_q[3]), .Qn(t_ff_11_qn), .reset(or_1_out));  // open: preset
  or or_1 (or_1_out, and_4_out, and_3_out);
  and and_3 (and_3_out, t_ff_3_q[2], t_ff_12_q[1]);
  and and_4 (and_4_out, t_ff_3_q[1], t_ff_3_q[3]);
  Hex_Digit_Display hex_digit_display_1 (.value({2'b00, t_ff_12_q}));  // open: dp
  Hex_Digit_Display hex_digit_display_2 (.value(t_ff_3_q));  // open: dp
  T_Flip_Flop t_ff_12 (
    .clk(t_ff_11_qn), .T(1'b1), .Q(t_ff_12_q[0]), .Qn(t_ff_12_qn), .reset(and_3_out));  // open: preset
  Hex_Digit_Display hex_digit_display_3 (.value(t_ff_1_q));  // open: dp
  Hex_Digit_Display hex_digit_display_4 (.value({1'b0, t_ff_2_q}));  // open: dp
  T_Flip_Flop t_ff_13 (.clk(t_ff_12_qn), .T(1'b1), .Q(t_ff_12_q[1]), .reset(and_3_out));  // open: Qn, preset
endmodule
