// Logisim project LicznikModulo16.circ as structural Verilog: 1 circuit, main circuit main
module main (
);

  wire and_1_out, and_2_out, and_3_out, and_4_out, and_5_out, and_6_out, and_7_out, and_8_out, and_9_out,
       clock_1_out, clock_2_out, d_ff_1_q, d_ff_1_qn, d_ff_2_q, d_ff_2_qn, d_ff_3_q, d_ff_3_qn, d_ff_4_q,
       d_ff_4_qn, or_1_out, or_2_out, or_3_out, t_ff_1_qn, t_ff_2_qn, t_ff_3_qn;
  wire [3:0] t_ff_1_q;

  and and_1 (and_1_out, d_ff_1_q, d_ff_4_qn);
  or or_1 (or_1_out, and_1_out, and_2_out, and_3_out);
  and and_2 (and_2_out, d_ff_1_q, d_ff_2_qn);
  and and_3 (and_3_out, d_ff_2_q, d_ff_3_q, d_ff_4_q);
  and and_4 (and_4_out, d_ff_2_q, d_ff_4_qn);
  or or_2 (or_2_out, and_4_out, and_5_out, and_6_out);
  and and_5 (and_5_out, d_ff_2_q, d_ff_3_qn);
  and and_6 (and_6_out, d_ff_1_qn, d_ff_2_qn, d_ff_3_q, d_ff_4_q);
  and and_7 (and_7_out, d_ff_3_qn, d_ff_4_q);
  or or_3 (or_3_out, and_7_out, and_8_out);
  // AND_Gate and_8 has open pins: out=and_8_out
  Clock clock_1 (.out(clock_1_out));
  D_Flip_Flop d_ff_1 (.clk(clock_1_out), .D(or_1_out), .Q(d_ff_1_q), .Qn(d_ff_1_qn));  // open: preset, reset
  D_Flip_Flop d_ff_2 (.clk(clock_1_out), .D(or_2_out), .Q(d_ff_2_q), .Qn(d_ff_2_qn));  // open: preset, reset
  D_Flip_Flop d_ff_3 (.clk(clock_1_out), .D(or_3_out), .Q(d_ff_3_q), .Qn(d_ff_3_qn));  // open: preset, reset
  D_Flip_Flop d_ff_4 (.clk(clock_1_out), .Q(d_ff_4_q), .Qn(d_ff_4_qn));  // open: D, preset, reset
  Clock clock_2 (.out(clock_2_out));
  T_Flip_Flop t_ff_1 (.clk(clock_2_out), .T(1'b1), .Q(t_ff_1_q[0]), .Qn(t_ff_1_qn), .reset(and_9_out));  // open: preset
  T_Flip_Flop t_ff_2 (.clk(t_ff_1_qn), .T(1'b1), .Q(t_ff_1_q[1]), .Qn(t_ff_2_qn), .reset(and_9_out));  // open: preset
  T_Flip_Flop t_ff_3 (.clk(t_ff_2_qn), .T(1'b1), .Q(t_ff_1_q[2]), .Qn(t_ff_3_qn), .reset(and_9_out));  // open: preset
  and and_9 (and_9_out, t_ff_1_q[2], t_ff_1_q[3]);
  T_Flip_Flop t_ff_4 (.clk(t_ff_3_qn), .T(1'b1), .Q(t_ff_1_q[3]), .reset(and_9_out));  // open: Qn, preset
  Hex_Digit_Display hex_digit_display_1 (.value(t_ff_1_q));  // open: dp
endmodule
