// Logisim project Odejmowanie_4_bit.circ as structural Verilog: 1 circuit, main circuit main
module main (
  input  in_1,
  input  A3,
  input  A2,
  input  A1,
  input  A0,
  input  B3,
  input  B2,
  input  B1,
  input  B0,
  input  C,
  input  B,
  input  A,
  output out_13,
  output out_14,
  output out_15,
  output out_16,
  output out_17,
  output out_18,
  output out_19
);

  wire and_1_out, and_2_out, and_3_out, and_4_out, and_5_out, and_6_out, and_7_out, and_8_out, and_9_out,
       and_10_out, and_11_out, and_12_out, and_13_out, and_14_out, and_15_out, not_1_out, not_2_out,
       not_3_out, not_4_out, not_5_out, not_6_out, not_7_out, not_8_out, not_9_out, not_10_out, or_1_out,
       or_3_out, or_4_out;

  not not_1 (not_1_out, A0);
  not not_2 (not_2_out, A0);
  and and_1 (and_1_out, B0, in_1);
  and and_2 (and_2_out, not_1_out, B0);
  and and_3 (and_3_out, not_2_out, in_1);
  or or_1 (or_1_out, and_2_out, and_3_out, and_1_out);
  not not_3 (not_3_out, A);
  not not_4 (not_4_out, A);
  and and_4 (and_4_out, not_4_out, C);
  and and_5 (and_5_out, not_3_out, B);
  or or_2 (out_19, and_5_out, and_4_out, and_6_out);
  xor xor_1 (out_16, in_1, B0, A0);
  and and_6 (and_6_out, B, C);
  not not_5 (not_5_out, A1);
  not not_6 (not_6_out, A1);
  and and_7 (and_7_out, not_5_out, or_1_out);
  and and_8 (and_8_out, not_6_out, B1);
  or or_3 (or_3_out, and_8_out, and_7_out, and_9_out);
  xor xor_2 (out_18, C, B, A);
  and and_9 (and_9_out, B1, or_1_out);
  xor xor_3 (out_15, or_1_out, B1, A1);
  not not_7 (not_7_out, A2);
  not not_8 (not_8_out, A2);
  and and_10 (and_10_out, not_8_out, or_3_out);
  and and_11 (and_11_out, B2, or_3_out);
  and and_12 (and_12_out, not_7_out, B2);
  or or_4 (or_4_out, and_12_out, and_10_out, and_11_out);
  xor xor_4 (out_14, or_3_out, B2, A2);
  not not_9 (not_9_out, A3);
  not not_10 (not_10_out, A3);
  and and_13 (and_13_out, not_10_out, B3);
  and and_14 (and_14_out, not_9_out, or_4_out);
  or or_5 (out_17, and_13_out, and_14_out, and_15_out);
  and and_15 (and_15_out, B3, or_4_out);
  xor xor_5 (out_13, or_4_out, B3, A3);

  // Notes on the sheet:
  //   Pożyczka
endmodule
