// Logisim project mnozator3bitczycos.circ as structural Verilog: 1 circuit, main circuit main
module main (
  input  in_1,
  input  in_2,
  input  in_3,
  input  in_4,
  output out_5,
  output out_6,
  output out_7,
  output out_8
);

  ROM #(.addrWidth(4), .dataWidth(4), .Select("low")) rom_1 (
    .addr({in_4, in_3, in_2, in_1}), .data({out_5, out_6, out_7, out_8}));

  // Notes on the sheet:
  //   contents of rom_1 (hex, n*v repeats v):
  //   5*0 1 2 3 0 2 4 6 0 3 6 9
endmodule
