// Logisim project asynchronicznymodulo6_025746.circ as structural Verilog: 1 circuit, main circuit main
module main (
  input  in_1,
  input  in_2
);

  wire or_1_out, t_ff_3_qn, t_ff_4_q, t_ff_4_qn, t_ff_5_q, t_ff_5_qn, t_ff_6_q, t_ff_6_qn, t_ff_8_qn;

  or or_1 (or_1_out, t_ff_4_qn, t_ff_6_q);
  T_Flip_Flop t_ff_1 ();  // open: clk, T, Q, Qn, preset, reset
  T_Flip_Flop t_ff_2 ();  // open: clk, T, Q, Qn, preset, reset
  T_Flip_Flop t_ff_3 (.Qn(t_ff_3_qn));  // open: clk, T, Q, preset, reset
  T_Flip_Flop t_ff_4 (.clk(t_ff_5_qn), .T(t_ff_6_qn), .Q(t_ff_4_q), .Qn(t_ff_4_qn));  // open: preset, reset
  T_Flip_Flop t_ff_5 (.clk(in_2), .T(1'b1), .Q(t_ff_5_q), .Qn(t_ff_5_qn));  // open: preset, reset
  T_Flip_Flop t_ff_6 (.clk(t_ff_5_qn), .T(or_1_out), .Q(t_ff_6_q), .Qn(t_ff_6_qn));  // open: preset, reset
  T_Flip_Flop t_ff_7 (.clk(t_ff_8_qn));  // open: T, Q, Qn, preset, reset
  T_Flip_Flop t_ff_8 (.clk(in_1), .Qn(t_ff_8_qn));  // open: T, Q, preset, reset
  T_Flip_Flop t_ff_9 (.clk(t_ff_8_qn));  // open: T, Q, Qn, preset, reset
endmodule
