// Logisim project egzamin_komparator.circ as structural Verilog: 1 circuit, main circuit main
module main (
  input  in_1,
  input  in_2,
  input  in_3,
  output out_4,
  output out_5
);

  wire and_1_out, and_2_out, and_3_out, and_4_out, not_1_out, not_2_out, not_3_out, not_4_out;

  not not_1 (not_1_out, in_1);
  not not_2 (not_2_out, in_2);
  not not_3 (not_3_out, in_2);
  not not_4 (not_4_out, in_1);
  and and_1 (and_1_out, not_1_out, in_2);
  and and_2 (and_2_out, in_1, not_2_out);
  and and_3 (and_3_out, in_1, not_3_out);
  and and_4 (and_4_out, not_4_out, in_2);
  J_K_Flip_Flop j_k_ff_1 (.J(and_1_out), .clk(in_3), .K(and_2_out), .Q(out_4));  // open: Qn, preset, reset
  J_K_Flip_Flop j_k_ff_2 (.J(and_3_out), .clk(in_3), .K(and_4_out), .Q(out_5));  // open: Qn, preset, reset
endmodule
