// Logisim project przerzutnik master-slave.circ as structural Verilog: 1 circuit, main circuit main
module main (
  input  in_1,
  input  in_2,
  output Q,
  output Q_prime,
  output Q_prime_2
);

  wire nand_1_out, nand_2_out, nand_3_out, nand_5_out, nand_6_out, not_1_out, not_2_out, not_3_out;

  not not_1 (not_1_out, in_2);
  not not_2 (not_2_out, in_1);
  nand nand_1 (nand_1_out, in_1, not_1_out);
  nand nand_2 (nand_2_out, not_1_out, not_2_out);
  nand nand_3 (nand_3_out, nand_1_out, Q_prime);
  nand nand_4 (Q_prime, nand_3_out, nand_2_out);
  not not_3 (not_3_out, nand_3_out);
  nand nand_5 (nand_5_out, nand_3_out, in_2);
  nand nand_6 (nand_6_out, in_2, not_3_out);
  nand nand_7 (Q, nand_5_out, Q_prime_2);
  nand nand_8 (Q_prime_2, Q, nand_6_out);

  // Notes on the sheet:
  //   D
  //   C
  //   Q
  //   D
  //   C
endmodule
