// Logisim project zatrzask bramkowany.circ as structural Verilog: 1 circuit, main circuit main
module main (
  input  in_1,
  input  in_2,
  input  in_3,
  input  D,
  input  C,
  output out_6,
  output out_7,
  output Q,
  output Q_prime
);

  wire nand_1_out, nand_2_out, nand_3_out, nand_4_out, not_1_out;

  not not_1 (not_1_out, D);
  nand nand_1 (nand_1_out, in_1, in_2);
  nand nand_2 (nand_2_out, in_2, in_3);
  nand nand_3 (nand_3_out, D, C);
  nand nand_4 (nand_4_out, C, not_1_out);
  nand nand_5 (out_6, nand_1_out, out_7);
  nand nand_6 (out_7, out_6, nand_2_out);
  nand nand_7 (Q, nand_3_out, Q_prime);
  nand nand_8 (Q_prime, Q, nand_4_out);
endmodule
